# Fritzing sketch montagem (saved by Fritzing 1.0.5)
breadboards: 1

parts:
  Componente1 = Arduino Uno (Rev3)
  S1 = Pushbutton [package="[SMD]"]
  R1 = Resistor [tolerance=±5% resistance=220 package="2512 [SMD]"]
  LED1 = smd LED [color="Red (633nm)" package="0805 [SMD]"]

nets:
  N1: Componente1.GND, S1.Pin_1, S1.Pin_2, R1.Pin_1
  N2: Componente1.D3_PWM, S1.Pin_3, S1.Pin_4
  N3: Componente1.D5_PWM, LED1.anode
  N4: R1.Pin_0, LED1.cathode
