# Fritzing sketch aula07_01 (saved by Fritzing 1.0.4)
breadboards: 1

parts:
  Componente2 = Arduino Uno (Rev3)
  J1 = Piezo Speaker
  R1 = Resistor [tolerance=±5% power=0.25W resistance=220 package=THT]

nets:
  N1: Componente2.D5_PWM, J1.pin2
  N2: Componente2.GND, R1.Pin_0
  N3: J1.pin1, R1.Pin_1
