# Fritzing sketch aula07_02 (saved by Fritzing 1.0.4)
breadboards: 1

parts:
  Componente3 = Arduino Uno (Rev3)
  PIR1 = PIR sensor

nets:
  N1: Componente3.D7, PIR1.SIG
  5V: Componente3.5V, PIR1.VDD
  GND: Componente3.GND, PIR1.GND

// code stored in the sketch: aula07_02.ino

