# Fritzing sketch circuito (saved by Fritzing 1.0.5)
breadboards: 1

parts:
  R1 = Photocell (LDR) [power=0.25W dark_resistance_@0.01lx=300kΩ light_resistance_@100lx=400Ω luminance=10lx package=THT]
  R2 = Resistor [tolerance=±5% resistance=1000 package="1206 [SMD]"]
  U1 = ESP32-38PinWide [part_number=ESP32-38PinWide]
  LED1 = smd LED [color="Red (633nm)" package="1206 [SMD]"]
  R3 = Resistor [tolerance=±5% resistance=220 package="1206 [SMD]"]

nets:
  N1: R1.pin_0, U1.GPIO11, R3.Pin_1
  N2: R1.pin_1, R2.Pin_0, U1.GPIO4
  N3: R2.Pin_1, U1.3.3
  N4: U1.GPIO26, LED1.anode
  N5: LED1.cathode, R3.Pin_0

custom parts:
  ESP32-38PinWide: Generic 38-Pin ESP32 with wide format (only access to one side of pins on a breadboard) based on Stephen Lilley's HiLetgo ESP-WROOM-32 ESP32 ESP-32S Development Board.
