# Fritzing sketch circuito1 (saved by Fritzing 1.0.5)
breadboards: 1

parts:
  U1 = ESP32-38PinWide [part_number=ESP32-38PinWide]
  A1 = DHT22 module

nets:
  N1: U1.3.3, A1.DAT
  N2: U1.GPIO27, A1.VCC
  N3: U1.GPIO11, A1.GND

custom parts:
  ESP32-38PinWide: Generic 38-Pin ESP32 with wide format (only access to one side of pins on a breadboard) based on Stephen Lilley's HiLetgo ESP-WROOM-32 ESP32 ESP-32S Development Board.
  DHT22 module: DHT22 module. Pins GND VCC Data.
