# Fritzing sketch circuito2 (saved by Fritzing 1.0.5)
breadboards: 1

parts:
  U1 = ESP32-38PinWide [part_number=ESP32-38PinWide]
  U2 = TRANSISTOR_NPN_2 [package=to-92]
  M1 = DC Motor [voltage_(max)=6V voltage_(min)=3V]
  R1 = Resistor [tolerance=±5% resistance=220 package="0402 [SMD]"]
  V1 = DC Power Supply [voltage=12V internal_resistance=1Ω max_current=0.1A]

nets:
  N1: U1.GPIO14, R1.Pin_0
  N2: U1.GPIO11, U2.E, V1.Pin_1
  N3: U2.C, M1.pin_2
  N4: U2.B, R1.Pin_1
  N5: M1.pin_1, V1.Pin_2

custom parts:
  ESP32-38PinWide: Generic 38-Pin ESP32 with wide format (only access to one side of pins on a breadboard) based on Stephen Lilley's HiLetgo ESP-WROOM-32 ESP32 ESP-32S Development Board.
